# Fritzing sketch Riego (saved by Fritzing 0.9.3b)
breadboards: 1

parts:
  Grove1 = Grove OLED 128x96
  Componente1 = Arduino Uno (Rev3)
  VCC1 = Battery block 9V
  KY-1 = Keyes Relay [package=THT]
  Part1 = Soil Moisture Sensor
  Part2 = Soil Moisture Sensor
  KY-2 = Keyes Relay [package=THT]
  S1 = SWITCH-MOMENTARY-2 [package=tactile-pth-12mm]
  S2 = SWITCH-MOMENTARY-2 [package=tactile-pth-12mm]
  hc-sr1 = hc-sr04
  ZS-042_RTC1 = ZS-042 RTC Module
  U1 = LM2596 step down module

nets:
  GND: Grove1.GND, Componente1.GND, KY-1.ground, Part1.GND, Part2.GND, KY-2.ground, hc-sr1.GND, ZS-042_RTC1.GND, U1.OUT-
  VCC: Grove1.VCC, Componente1.5V, KY-1.power, Part1.VCC, Part2.VCC, KY-2.power, S1.1, S2.1, hc-sr1.VCC, ZS-042_RTC1.VCC
  N1: Grove1.SDA, Componente1.A4/SDA, ZS-042_RTC1.SDA
  N2: Grove1.SCL, Componente1.A5/SCL, ZS-042_RTC1.SCL
  N3: Componente1.A0, Part2.SIG
  N4: Componente1.A1, Part1.SIG
  N5: Componente1.D8, S1.2
  N6: Componente1.D11_PWM/MOSI, hc-sr1.Echo
  N7: Componente1.D12/MISO, hc-sr1.Trig
  N8: Componente1.D2, KY-1.signal
  N9: Componente1.D4, KY-2.signal
  N10: Componente1.D7, S2.2
  N11: Componente1.VIN, U1.OUT+
  N12: VCC1.+, KY-1.C

custom parts:
  Keyes Relay: The Keyes 5V relay module is suitable for SCM development, home appliance control. It uses a 5V~12V TIL control signal which can control DC / AC signal.
  LM2596 step down module: LM2596 DC-DC step down power supply module 3 A.

// code stored in the sketch: Automatic Water.ino
#include <HCSR04.h>  //https://github.com/gamegine/HCSR04-ultrasonic-sensor-lib
#include <OLED_I2C.h>
#include <RTClib.h>

//  DEFAULT VARIABLES
const unsigned long minutes = 60 * 1000;

//  VARIABLES TO DEFINE
const DateTime currentTime(2019, 11, 22, 20, 45, 0);

//  Resistence sensor
const int minSoilMoisture = 15000; // ohmios

//  Tank height
const int sizeTank = 90; // cm

//  water periods
const int waterPeriod = 4 * minutes;  // minutes
const int waitWaterPeriod = 10 * minutes;  // minutes

//  water schedules
const int waterSchedules[2][2] = {{7, 0}, {18, 0}};


//  PIN USED
#define moisterSensor1_pin A0
#define moisterSensor2_pin A1

//#define  OLED SDA A4
//#define  OLED SCL A5

#define relay_pump_pin 2

#define relay_display_pin 4

#define button_display_pin 7
#define button_pump_pin 8

#define sensor_ultra1_echo_pin 11
#define sensor_ultra1_trig_pin 12

//  RTC
RTC_DS3231 rtc;

//  DISPLAY
OLED myOLED(SDA, SCL);
extern uint8_t TinyFont[];
extern uint8_t SmallFont[];
extern uint8_t MediumNumbers[];
extern uint8_t BigNumbers[];

//  ULTRASONIC SENSOR
HCSR04 hc(sensor_ultra1_trig_pin, sensor_ultra1_echo_pin); //initialisation class HCSR04 (trig pin , echo pin)

//  MENU OLED
//  1 - OLED ON AND DATE TIME
//  2 - SHOW LATEST WATER TIMES
//  3 - READ SENSORS
//  default - OLED OFF
int screenMenuSelector = 0;
const int screenNumberOptions = 3;

//  WATER
const int numberWaterRegisters = 5;
int waterRegisters[numberWaterRegisters][6];
int waterRegistersPointer = 0;

//  MENU PUMP
//  1 - PUMP ON
//  default - PUMP OFF
int pumpMenuSelector = 0;
const int pumpMenuOptions = 1;


unsigned long referenceTime;

void setup()
{
  Serial.begin(9600);

  //  RTC
  if (!rtc.begin()) {
    Serial.println("Module RTC no encontrado");
    while (1);
  }
  rtc.adjust(currentTime);

  //  PINS
  pinMode(relay_pump_pin, OUTPUT);
  pinMode(relay_display_pin, OUTPUT);
  pinMode(moisterSensor1_pin, INPUT);
  pinMode(moisterSensor2_pin, INPUT);
  pinMode(button_display_pin, INPUT);
  pinMode(button_pump_pin, INPUT);
}

void loop()
{
  pumpController();
  screenController();
  automaticWater();
}

/**
    Condition to water
    - Water in the tank
    - Morning/Evening water time
    - soil dry
*/
void automaticWater() {
  if (hc.dist() < sizeTank) { // tank with water
    DateTime now = rtc.now();
    for (int i = 0; i < sizeof waterSchedules / sizeof waterSchedules[0]; i++) { //  Times scheduled

      if (waterSchedules[i][0] == now.hour()) {

        int sensor1 = analogRead(moisterSensor1_pin);
        int sensor2 = analogRead(moisterSensor2_pin);

        if ((relay_pump_pin == LOW)                                     //  pump not active
            && (sensor1 > minSoilMoisture || sensor2 > minSoilMoisture) //  check moisture
            && ((millis() - referenceTime) > waitWaterPeriod)) {        //  latest water > 'waitWaterPeriod'

          referenceTime = millis(); //  save current time
          digitalWrite(relay_pump_pin, HIGH); // start water
          saveDateTime();
        }

        //  water for the 'waterPeriod' time
        if ((relay_pump_pin == HIGH) && ((millis() - referenceTime) > waterPeriod)) {  //  time watering
          digitalWrite(relay_pump_pin, LOW);
          referenceTime = millis();
        }
      }
    }
  }
}

/**
    Manual pump control
*/
void pumpController() {
  int waterButton = digitalRead(button_pump_pin);
  if (waterButton == HIGH) {
    while (waterButton == HIGH); //  Only 1 click
    pumpMenuSelector++;
    if (pumpMenuSelector > pumpMenuOptions) {
      screenMenuSelector = 0;
    }

    switch (pumpMenuSelector) {
      case 1: //  PUMP ON
        digitalWrite(relay_pump_pin, HIGH);
        saveDateTime();
        break;
      default: //  OLED OFF
        digitalWrite(relay_display_pin, LOW);
        break;
    }
  }
}

/**

*/
void screenController() {

  int displayButton = digitalRead(button_display_pin);
  if (displayButton == HIGH) {
    while (displayButton == HIGH);//  Only 1 click
    screenMenuSelector++;
    if (screenMenuSelector > screenNumberOptions) {
      screenMenuSelector = 0;
    }

    switch (screenMenuSelector) {
      case 1: //  OLED ON
        digitalWrite(relay_display_pin, HIGH);
        myOLED.begin();
        delay(2000); // wait 2s
          printClock();
        break;
      case 2:
        printLatestWater();
        break;
      case 3: //  TODO Display Sensors moisture, Tank water and RTC Temp
        //        printSersorData();
        break;
      default: //  OLED OFF

        digitalWrite(relay_display_pin, LOW);
        break;
    }
  }
}

/**
    Save the DateTime in numberWaterRegisters  2Darray
*/
void saveDateTime() {
  waterRegistersPointer++;
  if (waterRegistersPointer == numberWaterRegisters) {
    waterRegistersPointer = 0;
  }

  DateTime now = rtc.now();
  waterRegisters[waterRegistersPointer][0] = now.day();
  waterRegisters[waterRegistersPointer][1] = now.month();
  waterRegisters[waterRegistersPointer][2] = now.year();
  waterRegisters[waterRegistersPointer][3] = now.hour();
  waterRegisters[waterRegistersPointer][4] = now.minute();
  waterRegisters[waterRegistersPointer][5] = now.second();

}

void printClock(){
  DateTime now = rtc.now();
  myOLED.setFont(MediumNumbers);                             
//  myOLED.setPixel(20,4);                           
  myOLED.printNumI(now.hour(), CENTER, 4);
  myOLED.print(':', CENTER, 4);
  myOLED.printNumI(now.minute(), CENTER, 4);
  myOLED.print(':', CENTER, 4);
  myOLED.printNumI(now.second(), CENTER, 4);
  
  myOLED.setFont(SmallFont);                            
  myOLED.setPixel(35,22);
  myOLED.printNumI(now.year(), CENTER, 4);
  myOLED.print('/', CENTER, 4);
  myOLED.printNumI(now.month(), CENTER, 4);
  myOLED.print('/', CENTER, 4);
  myOLED.printNumI(now.day(), CENTER, 4);
  myOLED.update();
  myOLED.clrScr();
}

void printLatestWater() {
  myOLED.setFont(SmallFont);

  //  Print lastest irrigation days sorted by day
  int dateShorted = waterRegistersPointer;
  for (int i = 0; i < numberWaterRegisters; ++i) {
    //  DATE
    if (waterRegisters[i][0] > 0) { // if contains data
      myOLED.printNumI(waterRegisters[dateShorted][0], LEFT, i * 10);
      myOLED.print("/", LEFT, i * 10);
      myOLED.printNumI(waterRegisters[dateShorted][1], LEFT, i * 10);
      myOLED.print("/", LEFT, i * 10);
      myOLED.printNumI(waterRegisters[dateShorted][2], LEFT, i * 10);
      myOLED.print("  ", LEFT, i * 10);
      //  TIME
      myOLED.printNumI(waterRegisters[dateShorted][3], LEFT, i * 10);
      myOLED.print(":", LEFT, i * 10);
      myOLED.printNumI(waterRegisters[dateShorted][4], LEFT, i * 10);
      myOLED.print(":", LEFT, i * 10);
      myOLED.printNumI(waterRegisters[dateShorted][5], LEFT, i * 10);
    }

    dateShorted--;
    if (dateShorted < 0) {
      dateShorted = numberWaterRegisters - 1;
    }
  }

  //  Display current temperature
  myOLED.drawLine(95, 0, 95, 63);
  myOLED.drawRect(100, 5, 125, 30);
  myOLED.printNumI(rtc.getTemperature(), 105, 10);
  myOLED.update();
  myOLED.clrScr();
}
